# Fritzing sketch All-in-one Prototype 1 (saved by Fritzing 0.9.3b)
breadboards: 1

parts:
  Part1 = Adafruit Metro with Headers [part_number="Adafruit #2488"]
  Part2 = NeoPixel NeoMatrix 8x8 [part_number=1487]
  S1 = Round Pushbutton
  S2 = Round Pushbutton
  LED1 = smd LED [color="Red (633nm)" package="0805 [SMD]"]
  LED2 = smd LED [color="Red (633nm)" package="0805 [SMD]"]
  R1 = Resistor [tolerance=±5% resistance=2.2k package="0402 [SMD]"]
  R2 = Resistor [tolerance=±5% resistance=470 package="0402 [SMD]"]
  R3 = Resistor [tolerance=±5% resistance=220 package="0402 [SMD]"]  # not connected
  R4 = Resistor [tolerance=±5% resistance=220 package="0402 [SMD]"]

nets:
  N1: Part1.IO5, S1.leg1
  N2: Part1.IO4, S2.leg1
  N3: Part1.IO3, LED2.anode
  N4: Part1.IO2, R4.Pin_1
  +5V: Part1.+5V, Part2.VDD
  GND: Part1.GND, Part2.GND, LED1.anode, R1.Pin_1, R2.Pin_1
  N5: Part2.IN, R4.Pin_0
  N6: S1.leg0, LED1.cathode, R2.Pin_0
  N7: S2.leg0, R1.Pin_0

custom parts:
  Adafruit Metro with Headers: We sure love the ATmega328 here at Adafruit, and we use them a lot for our own projects. The processor has plenty of GPIO, Analog inputs, hardware UART SPI and I2C, timers and PWM galore - just enough for most simple projects. When we need to go small, we use a Pro Trinket 3V or 5V, but when size isn't as much of a concern, and an USB-serial converter is required, we reach for an Adafruit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
  NeoPixel NeoMatrix 8x8: Put on your sunglasses before wiring up this LED matrix - 64 eye-blistering RGB LEDs adorn the NeoMatrix for a blast of configurable color. Arranged in an 8x8 matrix, each pixel is individually addressable. Only one microcontroller pin is required to control all the LEDs, and you get 24 bit color for each LED.
