# Fritzing sketch Light Panel - Metro (saved by Fritzing 0.9.3b)
circuit board: 4.94329cm x 4.39836cm
breadboards: 1

parts:
  Part1 = NeoPixel NeoMatrix 8x8 [part_number=1487]
  Part2 = Adafruit HUZZAH ESP8266 [part_number="Adafruit #2471"]
  R1 = Resistor [tolerance=±5% resistance=470 package=THT]
  Part3 = Adafruit Metro with Headers [part_number="Adafruit #2488"]
  R2 = Resistor [tolerance=±5% resistance=470 package=THT]
  R3 = Resistor [tolerance=±5% resistance=470 package=THT]

nets:
  N1: Part1.IN, R1.Pin_0
  VDD: Part1.VDD, Part2.VIN, Part3.+5V
  GND: Part1.GND, Part2.GND, Part3.GND
  N2: Part2.GPIO4, R2.Pin_0
  N3: Part2.GPIO5, R3.Pin_0
  N4: R1.Pin_1, Part3.IO2
  N5: Part3.IO5, R3.Pin_1
  N6: Part3.IO4, R2.Pin_1

custom parts:
  NeoPixel NeoMatrix 8x8: Put on your sunglasses before wiring up this LED matrix - 64 eye-blistering RGB LEDs adorn the NeoMatrix for a blast of configurable color. Arranged in an 8x8 matrix, each pixel is individually addressable. Only one microcontroller pin is required to control all the LEDs, and you get 24 bit color for each LED.
  Adafruit HUZZAH ESP8266: Add Internet to your next project with an adorable, bite-sized WiFi microcontroller, at a price you like! The ESP8266 processor from Espressif is an 80 MHz microcontroller with a full WiFi front-end (both as client and access point) and TCP/IP stack with DNS support as well. While this chip has been very popular, its also been very difficult to use. Most of the low cost modules are not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
  Adafruit Metro with Headers: We sure love the ATmega328 here at Adafruit, and we use them a lot for our own projects. The processor has plenty of GPIO, Analog inputs, hardware UART SPI and I2C, timers and PWM galore - just enough for most simple projects. When we need to go small, we use a Pro Trinket 3V or 5V, but when size isn't as much of a concern, and an USB-serial converter is required, we reach for an Adafruit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
