# Fritzing sketch Light Panel (saved by Fritzing 0.9.3b)
circuit board: 4.94329cm x 4.39836cm
breadboards: 1

parts:
  Part1 = NeoPixel NeoMatrix 8x8 [part_number=1487]
  Part2 = Adafruit HUZZAH ESP8266 [part_number="Adafruit #2471"]
  U1 = 74AHCT125 [part_number=SN74AHCT125 package=dil14]
  J1 = Piezo Speaker
  Power_plug1 = Power plug
  R1 = Resistor [tolerance=±5% resistance=220 package=THT]
  R2 = Resistor [tolerance=±5% resistance=220 package=THT]

nets:
  N1: Part1.IN, U1.4Y
  VCC: Part1.VDD, Part2.VIN, U1.VCC, Power_plug1.VCC
  N2: Part1.GND, R1.Pin_0
  GND: Part2.GND, U1.GND, U1.3OE, U1.4OE, Power_plug1.GND, R1.Pin_1, R2.Pin_1
  N3: Part2.GPIO4, U1.3A
  N4: Part2.GPIO5, U1.4A
  N5: U1.3Y, J1.pin2
  N6: J1.pin1, R2.Pin_0

custom parts:
  NeoPixel NeoMatrix 8x8: Put on your sunglasses before wiring up this LED matrix - 64 eye-blistering RGB LEDs adorn the NeoMatrix for a blast of configurable color. Arranged in an 8x8 matrix, each pixel is individually addressable. Only one microcontroller pin is required to control all the LEDs, and you get 24 bit color for each LED.
  Adafruit HUZZAH ESP8266: Add Internet to your next project with an adorable, bite-sized WiFi microcontroller, at a price you like! The ESP8266 processor from Espressif is an 80 MHz microcontroller with a full WiFi front-end (both as client and access point) and TCP/IP stack with DNS support as well. While this chip has been very popular, its also been very difficult to use. Most of the low cost modules are not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
  74AHCT125: Quad Level-Shifter (3V to 5V) Quadruple Bus Buffer Gates With 3-State Outputs
